// Logisim project adders.circ as structural Verilog
module adder_1b (
  input  a,
  input  b,
  output s,
  output c_out
);

  and and_1 (c_out, a, b);
  xor xor_1 (s, a, b);
endmodule

module full_adder (
  input  a,
  input  b,
  input  c_in,
  output s,
  output c_out
);

  wire adder_1b_1_c_out, adder_1b_1_s, adder_1b_2_c_out;

  adder_1b adder_1b_1 (.a(a), .b(b), .s(adder_1b_1_s), .c_out(adder_1b_1_c_out));
  adder_1b adder_1b_2 (.a(adder_1b_1_s), .b(c_in), .s(s), .c_out(adder_1b_2_c_out));
  or or_1 (c_out, adder_1b_2_c_out, adder_1b_1_c_out);
endmodule

module rca_4b (
  input  c_in,
  input  x0,
  input  y0,
  input  x1,
  input  y1,
  input  x2,
  input  y2,
  input  x3,
  input  y3,
  output s0,
  output s1,
  output s2,
  output s3,
  output c_out
);

  wire full_adder_1_c_out, full_adder_2_c_out, full_adder_3_c_out;

  full_adder full_adder_1 (.a(x0), .b(y0), .c_in(c_in), .s(s0), .c_out(full_adder_1_c_out));
  full_adder full_adder_2 (.a(x1), .b(y1), .c_in(full_adder_1_c_out), .s(s1), .c_out(full_adder_2_c_out));
  full_adder full_adder_3 (.a(x2), .b(y2), .c_in(full_adder_2_c_out), .s(s2), .c_out(full_adder_3_c_out));
  full_adder full_adder_4 (.a(x3), .b(y3), .c_in(full_adder_3_c_out), .s(s3), .c_out(c_out));
endmodule

module addsub_1b (
  input  a,
  input  b,
  input  op,
  output s,
  output c_out
);

  wire not_1_out, xor_1_out;

  not not_1 (not_1_out, op);
  xor xor_1 (xor_1_out, b, not_1_out);
  full_adder full_adder_1 (.a(a), .b(xor_1_out), .c_in(not_1_out), .s(s), .c_out(c_out));
endmodule

module rc_addsub_4b (
  input  op,
  input  y0,
  input  x0,
  input  y1,
  input  x1,
  input  y2,
  input  x2,
  input  y3,
  input  x3,
  output s0,
  output s1,
  output s2,
  output s3,
  output c_out
);

  wire full_adder_1_c_out, full_adder_2_c_out, full_adder_3_c_out, not_1_out, xor_1_out, xor_2_out,
       xor_3_out, xor_4_out;

  not not_1 (not_1_out, op);
  xor xor_1 (xor_1_out, y0, not_1_out);
  xor xor_2 (xor_2_out, y1, not_1_out);
  xor xor_3 (xor_3_out, y2, not_1_out);
  xor xor_4 (xor_4_out, y3, not_1_out);
  full_adder full_adder_1 (.a(x0), .b(xor_1_out), .c_in(not_1_out), .s(s0), .c_out(full_adder_1_c_out));
  full_adder full_adder_2 (.a(x1), .b(xor_2_out), .c_in(full_adder_1_c_out), .s(s1), .c_out(full_adder_2_c_out));
  full_adder full_adder_3 (.a(x2), .b(xor_3_out), .c_in(full_adder_2_c_out), .s(s2), .c_out(full_adder_3_c_out));
  full_adder full_adder_4 (.a(x3), .b(xor_4_out), .c_in(full_adder_3_c_out), .s(s3), .c_out(c_out));
endmodule
