// Logisim project Ex01.circ as structural Verilog: 1 circuit, main circuit main
module main (
  input  A,
  input  B,
  input  C,
  input  Clock,
  output out_5
);

  wire and_1_out, and_2_out, d_ff_1_qn, or_1_out;

  and and_1 (and_1_out, A, B);
  D_Flip_Flop d_ff_1 (.D(and_2_out), .clk(Clock), .Q(out_5), .Qn(d_ff_1_qn));  // open: preset, reset
  and and_2 (and_2_out, or_1_out, d_ff_1_qn);
  or or_1 (or_1_out, and_1_out, C);
endmodule
